// Logisim project D8421+5.circ as structural Verilog: 1 circuit, main circuit main
module main (
  input  [3:0] in_1,
  output [3:0] out_2
);

  wire and_3_out, and_4_out, not_1_out, not_2_out, not_3_out, not_4_out, not_5_out, not_6_out, not_7_out,
       not_8_out, not_9_out, not_10_out, not_11_out, or_1_out, or_2_out, or_3_out, or_4_out, or_5_out,
       or_6_out, or_7_out;

  not not_1 (not_1_out, in_1[0]);
  not not_2 (not_2_out, in_1[1]);
  not not_3 (not_3_out, in_1[3]);
  not not_4 (not_4_out, in_1[2]);
  not not_5 (not_5_out, in_1[3]);
  or or_1 (or_1_out, not_1_out, not_2_out, not_3_out);
  or or_2 (or_2_out, not_4_out, not_5_out);
  or or_3 (or_3_out, in_1[3], in_1[2], in_1[1]);
  or or_4 (or_4_out, in_1[3], in_1[2], in_1[0]);
  and and_1 (out_2[3], or_1_out, or_2_out, or_3_out, or_4_out);
  not not_6 (not_6_out, in_1[1]);
  or or_5 (or_5_out, in_1[2], not_6_out, not_7_out);
  not not_7 (not_7_out, in_1[0]);
  not not_8 (not_8_out, in_1[2]);
  or or_6 (or_6_out, not_8_out, in_1[1]);
  not not_9 (not_9_out, in_1[2]);
  or or_7 (or_7_out, not_9_out, in_1[0]);
  and and_2 (out_2[2], or_5_out, or_6_out, or_7_out);
  not not_10 (not_10_out, in_1[1]);
  not not_11 (not_11_out, in_1[0]);
  and and_3 (and_3_out, in_1[0], not_10_out);
  and and_4 (and_4_out, in_1[1], not_11_out);
  or or_8 (out_2[1], and_3_out, and_4_out);
  not not_12 (out_2[0], in_1[0]);
endmodule
