// Logisim project ODS_3.circ as structural Verilog: 1 circuit, main circuit main
module main (
  input  [7:0] in_1,
  input  [7:0] in_2,
  input  in_3,
  input  [7:0] in_4,
  input  in_5,
  output [7:0] out_6,
  output [7:0] out_7
);

  wire not_1_out, not_2_out, not_3_out, not_4_out, not_5_out, not_6_out, not_7_out, not_8_out, not_9_out,
       not_10_out, not_11_out, not_12_out, not_13_out, not_14_out, not_15_out, not_16_out, not_17_out,
       not_18_out, not_19_out, not_20_out, not_21_out, not_22_out, not_23_out, not_24_out, not_25_out,
       not_26_out, not_27_out, not_28_out, not_29_out, not_30_out, not_31_out, not_32_out, not_33_out,
       not_34_out, not_35_out, not_36_out, not_37_out, not_38_out, not_39_out, not_40_out, not_41_out,
       not_42_out, not_43_out, not_44_out, not_45_out, not_46_out, not_47_out, not_48_out, not_49_out,
       not_50_out, not_51_out, not_52_out, not_53_out, not_54_out, not_55_out, not_56_out, not_57_out,
       not_58_out, not_59_out, not_60_out, not_61_out, not_62_out, not_63_out, not_64_out, not_65_out,
       not_66_out, not_67_out, not_68_out, not_69_out, not_70_out, not_71_out, not_72_out, not_73_out,
       not_74_out, not_75_out, not_76_out, not_77_out, not_78_out, not_79_out, not_80_out, not_81_out,
       not_82_out, not_83_out, not_84_out, not_85_out, not_86_out, not_87_out, not_88_out, not_89_out,
       not_90_out, not_91_out, not_92_out, not_93_out, not_94_out, not_95_out, not_96_out, or_1_out,
       or_2_out, or_3_out, or_4_out, or_5_out, or_6_out, or_7_out, or_8_out, or_9_out, or_10_out, or_11_out,
       or_12_out, or_13_out, or_14_out, or_15_out, or_16_out, or_17_out, or_18_out, or_19_out, or_20_out,
       or_21_out, or_22_out, or_23_out, or_24_out, or_25_out, or_26_out, or_27_out, or_28_out, or_29_out,
       or_30_out, or_31_out, or_32_out, or_33_out, or_34_out, or_35_out, or_36_out, or_37_out, or_38_out,
       or_39_out, or_40_out, or_41_out, or_42_out, or_43_out, or_44_out, or_45_out, or_46_out, or_47_out,
       or_48_out, or_49_out, or_50_out, or_51_out, or_52_out, or_53_out, or_54_out, or_55_out, or_56_out,
       or_57_out, or_58_out, or_59_out, or_60_out, or_61_out, or_62_out, or_63_out, or_64_out, or_65_out,
       or_66_out, or_67_out, or_68_out, or_69_out, or_70_out, or_71_out, or_72_out, or_73_out, or_74_out,
       or_75_out, or_76_out, or_77_out, or_78_out, or_79_out, or_80_out, or_81_out, or_82_out, or_83_out,
       or_84_out, or_85_out, or_86_out, or_87_out, or_88_out, or_89_out, or_90_out, or_91_out, or_92_out,
       or_93_out, or_94_out, or_95_out, or_96_out, or_97_out, or_98_out, or_99_out, or_100_out, or_101_out,
       or_102_out, or_103_out, or_104_out, or_105_out, or_106_out, or_107_out, or_108_out, or_109_out,
       or_110_out, or_111_out, or_112_out, P_2_out, P_3_out, P_4_out, P_5_out, P_6_out, P_7_out, P_8_out,
       P_9_out, P_10_out, P_11_out, P_12_out, P_13_out, P_14_out, P_15_out, P_16_out, P_out;

  or or_1 (or_1_out, in_1[0], in_2[0], in_3);
  not not_1 (not_1_out, in_1[0]);
  not not_2 (not_2_out, in_3);
  or or_2 (or_2_out, in_1[0], not_3_out, not_4_out);
  not not_3 (not_3_out, in_2[0]);
  not not_4 (not_4_out, in_3);
  not not_5 (not_5_out, in_4[0]);
  not not_6 (not_6_out, in_5);
  or or_3 (or_3_out, out_6[7], in_4[0], in_5);
  not not_7 (not_7_out, in_1[0]);
  not not_8 (not_8_out, in_2[0]);
  or or_4 (or_4_out, not_1_out, in_2[0], not_2_out);
  not not_9 (not_9_out, out_6[7]);
  not not_10 (not_10_out, in_4[0]);
  not not_11 (not_11_out, out_6[7]);
  or or_5 (or_5_out, not_11_out, in_4[0], not_12_out);
  not not_12 (not_12_out, in_5);
  or or_6 (or_6_out, out_6[7], not_5_out, not_6_out);
  or or_7 (or_7_out, not_7_out, not_8_out, in_3);
  and S (out_6[0], or_7_out, or_4_out, or_2_out, or_1_out);
  or or_8 (or_8_out, not_9_out, not_10_out, in_5);
  and S_2 (out_7[0], or_8_out, or_5_out, or_6_out, or_3_out);
  or or_9 (or_9_out, in_1[0], in_2[0]);
  or or_10 (or_10_out, in_1[0], in_3);
  or or_11 (or_11_out, in_2[0], in_3);
  or or_12 (or_12_out, out_6[7], in_4[0]);
  or or_13 (or_13_out, out_6[7], in_5);
  or or_14 (or_14_out, in_4[0], in_5);
  and P (P_out, or_9_out, or_10_out, or_11_out);
  and P_2 (P_2_out, or_12_out, or_13_out, or_14_out);
  not not_13 (not_13_out, in_1[1]);
  not not_14 (not_14_out, P_out);
  not not_15 (not_15_out, in_2[1]);
  not not_16 (not_16_out, P_out);
  or or_15 (or_15_out, in_1[1], in_2[1], P_out);
  not not_17 (not_17_out, in_4[1]);
  not not_18 (not_18_out, P_2_out);
  or or_16 (or_16_out, out_6[6], in_4[1], P_2_out);
  not not_19 (not_19_out, in_1[1]);
  not not_20 (not_20_out, in_2[1]);
  or or_17 (or_17_out, not_13_out, in_2[1], not_14_out);
  or or_18 (or_18_out, in_1[1], not_15_out, not_16_out);
  not not_21 (not_21_out, out_6[6]);
  not not_22 (not_22_out, in_4[1]);
  not not_23 (not_23_out, out_6[6]);
  or or_19 (or_19_out, not_23_out, in_4[1], not_24_out);
  not not_24 (not_24_out, P_2_out);
  or or_20 (or_20_out, out_6[6], not_17_out, not_18_out);
  or or_21 (or_21_out, not_19_out, not_20_out, P_out);
  or or_22 (or_22_out, not_21_out, not_22_out, P_2_out);
  and S_3 (out_6[1], or_21_out, or_17_out, or_18_out, or_15_out);
  and S_4 (out_7[1], or_22_out, or_19_out, or_20_out, or_16_out);
  or or_23 (or_23_out, in_1[1], in_2[1]);
  or or_24 (or_24_out, in_1[1], P_out);
  or or_25 (or_25_out, in_2[1], P_out);
  and P_3 (P_3_out, or_23_out, or_24_out, or_25_out);
  or or_26 (or_26_out, out_6[6], in_4[1]);
  or or_27 (or_27_out, out_6[6], P_2_out);
  or or_28 (or_28_out, in_4[1], P_2_out);
  and P_4 (P_4_out, or_26_out, or_27_out, or_28_out);
  not not_25 (not_25_out, in_1[2]);
  not not_26 (not_26_out, P_3_out);
  not not_27 (not_27_out, in_2[2]);
  not not_28 (not_28_out, P_3_out);
  or or_29 (or_29_out, in_1[2], in_2[2], P_3_out);
  not not_29 (not_29_out, in_4[2]);
  not not_30 (not_30_out, P_4_out);
  or or_30 (or_30_out, out_6[5], in_4[2], P_4_out);
  not not_31 (not_31_out, in_1[2]);
  not not_32 (not_32_out, in_2[2]);
  or or_31 (or_31_out, not_25_out, in_2[2], not_26_out);
  or or_32 (or_32_out, in_1[2], not_27_out, not_28_out);
  not not_33 (not_33_out, out_6[5]);
  not not_34 (not_34_out, in_4[2]);
  not not_35 (not_35_out, out_6[5]);
  or or_33 (or_33_out, not_35_out, in_4[2], not_36_out);
  not not_36 (not_36_out, P_4_out);
  or or_34 (or_34_out, out_6[5], not_29_out, not_30_out);
  or or_35 (or_35_out, not_31_out, not_32_out, P_3_out);
  or or_36 (or_36_out, not_33_out, not_34_out, P_4_out);
  and S_5 (out_6[2], or_35_out, or_31_out, or_32_out, or_29_out);
  and S_6 (out_7[2], or_36_out, or_33_out, or_34_out, or_30_out);
  or or_37 (or_37_out, in_1[2], in_2[2]);
  or or_38 (or_38_out, in_1[2], P_3_out);
  or or_39 (or_39_out, in_2[2], P_3_out);
  and P_5 (P_5_out, or_37_out, or_38_out, or_39_out);
  or or_40 (or_40_out, out_6[5], in_4[2]);
  or or_41 (or_41_out, out_6[5], P_4_out);
  or or_42 (or_42_out, in_4[2], P_4_out);
  and P_6 (P_6_out, or_40_out, or_41_out, or_42_out);
  not not_37 (not_37_out, in_1[3]);
  not not_38 (not_38_out, P_5_out);
  not not_39 (not_39_out, in_2[3]);
  not not_40 (not_40_out, P_5_out);
  or or_43 (or_43_out, in_1[3], in_2[3], P_5_out);
  not not_41 (not_41_out, in_4[3]);
  not not_42 (not_42_out, P_6_out);
  or or_44 (or_44_out, out_6[4], in_4[3], P_6_out);
  not not_43 (not_43_out, in_1[3]);
  not not_44 (not_44_out, in_2[3]);
  or or_45 (or_45_out, not_37_out, in_2[3], not_38_out);
  or or_46 (or_46_out, in_1[3], not_39_out, not_40_out);
  not not_45 (not_45_out, out_6[4]);
  not not_46 (not_46_out, in_4[3]);
  not not_47 (not_47_out, out_6[4]);
  or or_47 (or_47_out, not_47_out, in_4[3], not_48_out);
  not not_48 (not_48_out, P_6_out);
  or or_48 (or_48_out, out_6[4], not_41_out, not_42_out);
  or or_49 (or_49_out, not_43_out, not_44_out, P_5_out);
  or or_50 (or_50_out, not_45_out, not_46_out, P_6_out);
  and S_7 (out_6[3], or_49_out, or_45_out, or_46_out, or_43_out);
  and S_8 (out_7[3], or_50_out, or_47_out, or_48_out, or_44_out);
  or or_51 (or_51_out, in_1[3], in_2[3]);
  or or_52 (or_52_out, in_1[3], P_5_out);
  or or_53 (or_53_out, in_2[3], P_5_out);
  and P_7 (P_7_out, or_51_out, or_52_out, or_53_out);
  or or_54 (or_54_out, out_6[4], in_4[3]);
  or or_55 (or_55_out, out_6[4], P_6_out);
  or or_56 (or_56_out, in_4[3], P_6_out);
  and P_8 (P_8_out, or_54_out, or_55_out, or_56_out);
  not not_49 (not_49_out, in_1[4]);
  not not_50 (not_50_out, P_7_out);
  not not_51 (not_51_out, in_2[4]);
  not not_52 (not_52_out, P_7_out);
  or or_57 (or_57_out, in_1[4], in_2[4], P_7_out);
  not not_53 (not_53_out, in_4[4]);
  not not_54 (not_54_out, P_8_out);
  or or_58 (or_58_out, out_6[3], in_4[4], P_8_out);
  not not_55 (not_55_out, in_1[4]);
  not not_56 (not_56_out, in_2[4]);
  or or_59 (or_59_out, not_49_out, in_2[4], not_50_out);
  or or_60 (or_60_out, in_1[4], not_51_out, not_52_out);
  not not_57 (not_57_out, out_6[3]);
  not not_58 (not_58_out, in_4[4]);
  not not_59 (not_59_out, out_6[3]);
  or or_61 (or_61_out, not_59_out, in_4[4], not_60_out);
  not not_60 (not_60_out, P_8_out);
  or or_62 (or_62_out, out_6[3], not_53_out, not_54_out);
  or or_63 (or_63_out, not_55_out, not_56_out, P_7_out);
  or or_64 (or_64_out, not_57_out, not_58_out, P_8_out);
  and S_9 (out_6[4], or_63_out, or_59_out, or_60_out, or_57_out);
  and S_10 (out_7[4], or_64_out, or_61_out, or_62_out, or_58_out);
  or or_65 (or_65_out, in_1[4], in_2[4]);
  or or_66 (or_66_out, in_1[4], P_7_out);
  or or_67 (or_67_out, in_2[4], P_7_out);
  and P_9 (P_9_out, or_65_out, or_66_out, or_67_out);
  or or_68 (or_68_out, out_6[3], in_4[4]);
  or or_69 (or_69_out, out_6[3], P_8_out);
  or or_70 (or_70_out, in_4[4], P_8_out);
  and P_10 (P_10_out, or_68_out, or_69_out, or_70_out);
  not not_61 (not_61_out, in_2[5]);
  not not_62 (not_62_out, P_9_out);
  or or_71 (or_71_out, in_1[5], in_2[5], P_9_out);
  not not_63 (not_63_out, in_4[5]);
  not not_64 (not_64_out, P_10_out);
  or or_72 (or_72_out, out_6[2], in_4[5], P_10_out);
  not not_65 (not_65_out, in_1[5]);
  not not_66 (not_66_out, in_2[5]);
  not not_67 (not_67_out, in_1[5]);
  or or_73 (or_73_out, not_67_out, in_2[5], not_68_out);
  not not_68 (not_68_out, P_9_out);
  or or_74 (or_74_out, in_1[5], not_61_out, not_62_out);
  not not_69 (not_69_out, out_6[2]);
  not not_70 (not_70_out, in_4[5]);
  not not_71 (not_71_out, out_6[2]);
  not not_72 (not_72_out, P_10_out);
  or or_75 (or_75_out, out_6[2], not_63_out, not_64_out);
  or or_76 (or_76_out, not_65_out, not_66_out, P_9_out);
  or or_77 (or_77_out, not_69_out, not_70_out, P_10_out);
  or or_78 (or_78_out, not_71_out, in_4[5], not_72_out);
  and S_11 (out_6[5], or_76_out, or_73_out, or_74_out, or_71_out);
  and S_12 (out_7[5], or_77_out, or_78_out, or_75_out, or_72_out);
  or or_79 (or_79_out, in_1[5], in_2[5]);
  or or_80 (or_80_out, in_1[5], P_9_out);
  or or_81 (or_81_out, in_2[5], P_9_out);
  and P_11 (P_11_out, or_79_out, or_80_out, or_81_out);
  or or_82 (or_82_out, out_6[2], in_4[5]);
  or or_83 (or_83_out, out_6[2], P_10_out);
  or or_84 (or_84_out, in_4[5], P_10_out);
  and P_12 (P_12_out, or_82_out, or_83_out, or_84_out);
  not not_73 (not_73_out, in_2[6]);
  not not_74 (not_74_out, P_11_out);
  or or_85 (or_85_out, in_1[6], in_2[6], P_11_out);
  not not_75 (not_75_out, in_4[6]);
  not not_76 (not_76_out, P_12_out);
  or or_86 (or_86_out, out_6[1], in_4[6], P_12_out);
  not not_77 (not_77_out, in_1[6]);
  not not_78 (not_78_out, in_2[6]);
  not not_79 (not_79_out, in_1[6]);
  or or_87 (or_87_out, not_79_out, in_2[6], not_80_out);
  not not_80 (not_80_out, P_11_out);
  or or_88 (or_88_out, in_1[6], not_73_out, not_74_out);
  not not_81 (not_81_out, out_6[1]);
  not not_82 (not_82_out, in_4[6]);
  not not_83 (not_83_out, out_6[1]);
  not not_84 (not_84_out, P_12_out);
  or or_89 (or_89_out, out_6[1], not_75_out, not_76_out);
  or or_90 (or_90_out, not_77_out, not_78_out, P_11_out);
  or or_91 (or_91_out, not_81_out, not_82_out, P_12_out);
  or or_92 (or_92_out, not_83_out, in_4[6], not_84_out);
  and S_13 (out_6[6], or_90_out, or_87_out, or_88_out, or_85_out);
  and S_14 (out_7[6], or_91_out, or_92_out, or_89_out, or_86_out);
  or or_93 (or_93_out, in_1[6], in_2[6]);
  or or_94 (or_94_out, in_1[6], P_11_out);
  or or_95 (or_95_out, in_2[6], P_11_out);
  and P_13 (P_13_out, or_93_out, or_94_out, or_95_out);
  or or_96 (or_96_out, out_6[1], in_4[6]);
  or or_97 (or_97_out, out_6[1], P_12_out);
  or or_98 (or_98_out, in_4[6], P_12_out);
  and P_14 (P_14_out, or_96_out, or_97_out, or_98_out);
  not not_85 (not_85_out, in_2[7]);
  not not_86 (not_86_out, P_13_out);
  or or_99 (or_99_out, in_1[7], in_2[7], P_13_out);
  not not_87 (not_87_out, in_4[7]);
  not not_88 (not_88_out, P_14_out);
  or or_100 (or_100_out, out_6[0], in_4[7], P_14_out);
  not not_89 (not_89_out, in_1[7]);
  not not_90 (not_90_out, in_2[7]);
  not not_91 (not_91_out, in_1[7]);
  not not_92 (not_92_out, P_13_out);
  or or_101 (or_101_out, in_1[7], not_85_out, not_86_out);
  not not_93 (not_93_out, out_6[0]);
  not not_94 (not_94_out, P_14_out);
  or or_102 (or_102_out, out_6[0], not_87_out, not_88_out);
  or or_103 (or_103_out, not_89_out, not_90_out, P_13_out);
  or or_104 (or_104_out, not_91_out, in_2[7], not_92_out);
  not not_95 (not_95_out, out_6[0]);
  or or_105 (or_105_out, not_95_out, not_96_out, P_14_out);
  not not_96 (not_96_out, in_4[7]);
  or or_106 (or_106_out, not_93_out, in_4[7], not_94_out);
  and S_15 (out_6[7], or_103_out, or_104_out, or_101_out, or_99_out);
  and S_16 (out_7[7], or_105_out, or_106_out, or_102_out, or_100_out);
  or or_107 (or_107_out, in_1[7], in_2[7]);
  or or_108 (or_108_out, in_1[7], P_13_out);
  or or_109 (or_109_out, in_2[7], P_13_out);
  or or_110 (or_110_out, out_6[0], in_4[7]);
  or or_111 (or_111_out, out_6[0], P_14_out);
  or or_112 (or_112_out, in_4[7], P_14_out);
  and P_15 (P_15_out, or_107_out, or_108_out, or_109_out);
  and P_16 (P_16_out, or_110_out, or_111_out, or_112_out);
endmodule
